# Fritzing sketch bt (saved by Fritzing 0.9.3b)
circuit board: 6cm x 6cm
breadboards: 1

parts:
  Part1 = Arduino Nano (Rev3.0) (ICSP)
  Part2 = Bluetooth HC-05 Macho
  IC1 = L293D [package=THT]
  J1 = Piezo Speaker
  VCC1 = Battery block 9V
  M1 = DC Motor
  M2 = DC Motor
  LED1 = smd LED [color="Red (633nm)" package="1206 [SMD]"]

nets:
  N1: Part1.D1/TX, Part2.RXD
  N2: Part1.D0/RX, Part2.TXD
  GND: Part1.GND, Part2.GND, IC1.0V, J1.pin1, VCC1.-
  N3: Part1.D8, IC1.In_4
  N4: Part1.D9, IC1.In_3
  N5: Part1.D10, J1.pin2
  N6: Part1.D11/MOSI, IC1.In_1
  N7: Part1.D12/MISO, IC1.In_2
  N8: Part1.VIN, IC1.+Vmotor, VCC1.+
  5V: Part1.5V, Part2.VCC
  N9: Part1.D13/SCK, LED1.anode
  N10: IC1.Enable_1, IC1.Enable_2, IC1.+V
  N11: IC1.Out_1_(_Controlled_by_Enable_1_), M2.pin_1
  N12: IC1.Out_2_(_Controlled_by_Enable_1_), M2.pin_2
  N13: IC1.Out_3_(_Controlled_by_Enable_2_), M1.pin_1
  N14: IC1.Out_4_(_Controlled_by_Enable_2_), M1.pin_2
